// Logisim project Circuitos Lógicos Aula 1.circ as structural Verilog: 3 circuits, main circuit main
module main (
  input  [3:0] in_1,
  input  [3:0] in_2,
  output out_3,
  output [3:0] out_4
);

  // Probe on in_1
  // Probe on in_2
  ADD4 add4_1 (.A(in_2), .B(in_1), .out_5(out_4), .out_4(out_3), .in_3(1'b0));
  // Probe on out_4
endmodule

module ADD1 (
  input  A,
  input  B,
  input  Vem1,
  output S,
  output Vai1
);

  wire and_1_out, and_2_out, and_3_out, xor_1_out;

  xor xor_1 (xor_1_out, A, B);
  and and_1 (and_1_out, A, Vem1);
  and and_2 (and_2_out, A, B);
  and and_3 (and_3_out, B, Vem1);
  xor xor_2 (S, xor_1_out, Vem1);
  or or_1 (Vai1, and_1_out, and_2_out, and_3_out);
endmodule

module ADD4 (
  input  [3:0] B,
  input  [3:0] A,
  input  in_3,
  output out_4,
  output [3:0] out_5
);

  wire add1_2_vai1, add1_3_vai1, add1_4_vai1;

  // Probe on B
  ADD1 add1_1 (.A(A[3]), .B(B[3]), .Vem1(add1_3_vai1), .S(out_5[3]), .Vai1(out_4));
  // Probe on out_5
  // Probe on A
  ADD1 add1_2 (.A(A[1]), .B(B[1]), .Vem1(add1_4_vai1), .S(out_5[1]), .Vai1(add1_2_vai1));
  ADD1 add1_3 (.A(A[2]), .B(B[2]), .Vem1(add1_2_vai1), .S(out_5[2]), .Vai1(add1_3_vai1));
  ADD1 add1_4 (.A(A[0]), .B(B[0]), .Vem1(in_3), .S(out_5[0]), .Vai1(add1_4_vai1));
endmodule
